# Fritzing sketch protoboard (saved by Fritzing 0.9.2b)

parts:
  Componente1 = Arduino Uno (Rev3)
  DHT1 = DHT11 Humitidy and Temperature Sensor
  DHT2 = DHT11 Humitidy and Temperature Sensor
  microSD1 = MicroSD Breakout
  RTC1 = DS1307 RTC Breakout

nets:
  N1: Componente1.A1, DHT1.DATA
  N2: Componente1.A2, DHT2.DATA
  N3: Componente1.A4/SDA, RTC1.SDA
  N4: Componente1.A5/SCL, RTC1.SCL
  N5: Componente1.D10_PWM/SS, microSD1.CS
  N6: Componente1.D11_PWM/MOSI, microSD1.DO
  N7: Componente1.D12/MISO, microSD1.DI
  N8: Componente1.D13/SCK, microSD1.CLK
  GND: Componente1.GND, DHT1.GND, DHT2.GND, microSD1.GND, RTC1.GND
  5V: Componente1.5V, DHT1.VDD, DHT2.VDD, microSD1.5V, RTC1.5V

custom parts:
  DHT11 Humitidy and Temperature Sensor: DHT11 Humidity and Temperature Sensor
  MicroSD Breakout: 5V-ready microSD Breakout with Level Shifter
  DS1307 RTC Breakout: DS1307 Real-time Clock Breakout Board with Battery
